# Fritzing sketch Sunshine (saved by Fritzing 0.9.3b)
breadboards: 1

parts:
  LED1 = LED - 3mm [color="Red (633nm)" package="3 mm [THT]"]
  Power_plug1 = Power plug
  S3 = Toggle Switch [package=THT]
  C1 = Capacitor Polarized [package=cpol-radial-1000uf-25v]
  C2 = Electrolytic Capacitor [capacitance=1000μF package="1010 [SMD, electrolytic]"]
  C3 = Capacitor [package=cap-pth-small2]
  S1 = Momentary Switch [package=ksa_sealed_tac_switch]
  C4 = Capacitor [package=cap-pth-small2]
  U1 = ESP8266 WiFi Module [part_number=ESP8266]
  Q1 = 2N7000 FET N-Channel [part_number=2N7000 package=TO92]
  U2 = Voltage Regulator - 5V [package="DPak [SMD]"]
  S4 = Toggle Switch [package=THT]
  J1 = female pin header, 2 pins [form="♀ (female)"]
  J2 = female pin header, 2 pins [form="♀ (female)"]
  J3 = female pin header, 2 pins [form="♀ (female)"]

nets (from the breadboard view):
  N1: LED1.cathode, Q1.drain, J1.pin1
  N2: LED1.anode, S3.COM, C1.+, C3.2, U2.input_voltage, J1.pin2
  GND: Power_plug1.GND, C1.-, C2.-, C3.1, S1.1, C4.1, U1.GND, Q1.source, U2.GND, S4.L1, J3.pin2
  N3: Power_plug1.VCC, S3.L1
  N4: C2.+, C4.2, U1.VCC, U1.CH_PD, U2.output_voltage
  N5: S1.4, U1.RST
  N6: U1.RXD, J2.pin1
  N7: U1.GPIO_0, S4.COM
  N8: U1.GPIO_2, Q1.gate
  N9: U1.TXD, J2.pin2

custom parts:
  ESP8266 WiFi Module: Generic WiFi Module based on the ESP8266 with onboard PCB antenna and UART communications
  2N7000 FET N-Channel: A 2N7000 MOSFET N-Channel Transistor
